# Fritzing sketch vitual_system (saved by Fritzing 0.9.3b)
breadboards: 2

parts:
  Part1 = Arduino Mega 2560 (Rev3)
  LCD1 = LCD screen
  LCM1602_IIC1 = LCM1602 IIC [part_number="LCM1602 IIC" chip_label="LCM1602 IIC" package="DIP (Dual Inline) [THT]"]
  SG2 = Buzzer 12mm [package=buzzer-12mm-ns]
  R1 = Resistor [tolerance=±5% resistance=10k package="0603 [SMD]"]
  R2 = Temperature Sensor (Thermistor) [thermistor_type=NTC package=THT]
  R3 = Resistor [tolerance=±5% resistance=3.3 package=THT]
  LED1 = LED - 5mm [color="Red (633nm)" package="5 mm [THT]"]
  R4 = Photocell (LDR) [package=THT]
  R5 = Resistor [tolerance=±5% resistance=10k package=THT]
  Keypad4x1 = Keypad Membran 4x4
  R6 = Photocell (LDR) [package=THT]
  R7 = Resistor [tolerance=±5% resistance=10k package="0603 [SMD]"]
  R8 = Resistor [tolerance=±5% resistance=330 package="0603 [SMD]"]
  R9 = Resistor [tolerance=±5% resistance=330 package="0603 [SMD]"]
  LED2 = LED - 5mm [color="Red (633nm)" package="5 mm [THT]"]
  LED3 = LED - 5mm [color="Red (633nm)" package="5 mm [THT]"]
  D1 = Rectifier Diode [part_number=1N4001 package="300 mil [THT]"]
  D2 = Rectifier Diode [part_number=1N4001 package="300 mil [THT]"]  # not connected
  Q1 = NPN-Transistor [package="TO92 [THT]"]
  Q2 = NPN-Transistor [package="TO92 [THT]"]
  M1 = DC Motor
  M2 = DC Motor
  R10 = Resistor [tolerance=±5% resistance=330 package=THT]
  R11 = Resistor [tolerance=±5% resistance=330 package=THT]
  U2 = ESP8266 WiFi Module [part_number=ESP8266]
  R12 = Resistor [tolerance=±5% resistance=330 package=THT]
  R13 = Resistor [tolerance=±5% resistance=330 package=THT]
  VCC1 = Battery

nets:
  N1: Part1.A0, R6.pin_0, R7.Pin_0
  N2: Part1.A2, R1.Pin_0, R2.pin_0
  N3: Part1.A3, R4.pin_0, R5.Pin_0
  N4: Part1.SCL, LCM1602_IIC1.SCL
  N5: Part1.SDA, LCM1602_IIC1.SDA
  N6: Part1.D13_PWM, R3.Pin_0
  N7: Part1.D12_PWM, SG2.1
  N8: Part1.D9_PWM, R8.Pin_0, R9.Pin_0
  5V: Part1.5V, LCM1602_IIC1.VCC, R2.pin_1, R4.pin_1, R6.pin_1, D1.cathode, M1.pin_2, M2.pin_2
  GND: Part1.GND, LCM1602_IIC1.GND, SG2.2, R1.Pin_1, LED1.cathode, R5.Pin_1, R7.Pin_1, LED2.cathode, LED3.cathode, Q1.E, Q2.E, U2.GND, VCC1.-
  N9: Part1.D3_PWM, R11.Pin_0
  N10: Part1.D4_PWM, R10.Pin_0
  N11: Part1.D22, Keypad4x1.Pin8
  N12: Part1.D24, Keypad4x1.Pin7
  N13: Part1.D26, Keypad4x1.Pin6
  N14: Part1.D28, Keypad4x1.Pin5
  N15: Part1.D30, Keypad4x1.Pin4
  N16: Part1.D32, Keypad4x1.Pin3
  N17: Part1.D34, Keypad4x1.Pin2
  N18: Part1.D36, Keypad4x1.Pin1
  VSS: LCD1.VSS, LCM1602_IIC1.VSS
  VDD: LCD1.VDD, LCM1602_IIC1.VDD
  N19: LCD1.V0, LCM1602_IIC1.V0
  N20: LCD1.RS, LCM1602_IIC1.RS
  N21: LCD1.R/W, LCM1602_IIC1.RW
  N22: LCD1.E, LCM1602_IIC1.E
  N23: LCD1.DB0, LCM1602_IIC1.D0
  N24: LCD1.DB1, LCM1602_IIC1.D1
  N25: LCD1.DB2, LCM1602_IIC1.D2
  N26: LCD1.DB3, LCM1602_IIC1.D3
  N27: LCD1.DB4, LCM1602_IIC1.D4
  N28: LCD1.DB5, LCM1602_IIC1.D5
  N29: LCD1.DB6, LCM1602_IIC1.D6
  N30: LCD1.DB7, LCM1602_IIC1.D7
  N31: LCD1.LED+, LCM1602_IIC1.A
  N32: LCD1.LED-, LCM1602_IIC1.K
  N33: LCM1602_IIC1.LED_A, LCM1602_IIC1.LED_B
  N34: R3.Pin_1, LED1.anode
  N35: R8.Pin_1, LED3.anode
  N36: R9.Pin_1, LED2.anode
  N37: D1.anode, Q2.C, M1.pin_1
  N38: Q1.B, R10.Pin_1
  N39: Q1.C, M2.pin_1
  N40: Q2.B, R11.Pin_1
  N41: U2.GPIO_0, R12.Pin_1
  N42: U2.GPIO_2, R13.Pin_1
  N43: R12.Pin_0, R13.Pin_0, VCC1.+

custom parts:
  LCM1602 IIC: I2C-Module to use a 1602 or 2004 LCD on with the wire.h libory Serial LCD Modul
  Keypad Membran 4x4: Membrane Keypad 4x4 Matrix
  ESP8266 WiFi Module: Generic WiFi Module based on the ESP8266 with onboard PCB antenna and UART communications
